// Logisim project Q1_CRC.circ as structural Verilog: 2 circuits, main circuit 4div4CRC
module _4div4CRC (
  input  [3:0] beichu,
  input  [3:0] chu,
  output shang,
  output [2:0] yu
);

  wire [3:0] xor_1_out;

  assign xor_1_out = beichu ^ chu;  // XOR_Gate xor_1, 4 bits wide
  Multiplexer #(.width(3)) multiplexer_1 (
    .in0(beichu[2:0]), .in1(xor_1_out[2:0]), .out(yu), .sel(beichu[3]));  // open: en

  assign shang = beichu[3];
endmodule

module CRC (
  input  [7:0] A,
  input  [3:0] B,
  output [10:0] C
);

  wire [2:0] half, n4div4crc_1_yu, n4div4crc_2_yu, n4div4crc_3_yu, n4div4crc_4_yu, n4div4crc_5_yu,
       n4div4crc_6_yu;

  _4div4CRC u_4div4crc_1 (.beichu({half, A[0]}), .chu(B), .yu(n4div4crc_1_yu));  // open: shang
  _4div4CRC u_4div4crc_2 (.beichu(A[7:4]), .chu(B), .yu(n4div4crc_2_yu));  // open: shang
  _4div4CRC u_4div4crc_3 (.beichu({n4div4crc_1_yu, 1'b0}), .chu(B), .yu(n4div4crc_3_yu));  // open: shang
  _4div4CRC u_4div4crc_4 (.beichu({n4div4crc_2_yu, A[3]}), .chu(B), .yu(n4div4crc_4_yu));  // open: shang
  _4div4CRC u_4div4crc_5 (.beichu({n4div4crc_3_yu, 1'b0}), .chu(B), .yu(n4div4crc_5_yu));  // open: shang
  _4div4CRC u_4div4crc_6 (.beichu({n4div4crc_4_yu, A[2]}), .chu(B), .yu(n4div4crc_6_yu));  // open: shang
  _4div4CRC u_4div4crc_7 (.beichu({n4div4crc_5_yu, 1'b0}), .chu(B), .yu(C[2:0]));  // open: shang
  _4div4CRC u_4div4crc_8 (.beichu({n4div4crc_6_yu, A[1]}), .chu(B), .yu(half));  // open: shang

  assign C[10:3] = A;

  // Other names for the same wires on the sheet: _0 = A[0]; _3 = A[3]; _2 = A[2]; _1 = A[1]; chu[3:0] = B
endmodule
