// Logisim project Q3_GRF.circ as structural Verilog: 2 circuits, main circuit grf
module grf (
  input  clk,
  input  reset,
  input  WE,
  input  [4:0] A1,
  input  [4:0] A2,
  input  [4:0] A3,
  input  [31:0] WD,
  output [31:0] RD1,
  output [31:0] RD2
);

  wire WE0, WE1, WE2, WE3, WE4, WE5, WE6, WE7, WE8, WE9, WE10, WE11, WE12, WE13, WE14, WE15, WE16, WE17,
       WE18, WE19, WE20, WE21, WE22, WE23, WE24, WE25, WE26, WE27, WE28, WE29, WE30, WE31;
  wire [31:0] _0, _1, _2, _3, _4, _5, _6, _7, _8, _9, _10, _11, _12, _13, _14, _15, _16, _17, _18, _19, _20,
       _21, _22, _23, _24, _25, _26, _27, _28, _29, _30, _31;

  get_WE get_we_1 (
    .WE(WE), .in_2(A3), .out_3(WE0), .out_4(WE1), .out_5(WE2), .out_6(WE3), .out_7(WE4), .out_8(WE5),
    .out_9(WE6), .out_10(WE7), .out_11(WE8), .out_12(WE9), .out_13(WE10), .out_14(WE11), .out_15(WE12),
    .out_16(WE13), .out_17(WE14), .out_18(WE15), .out_19(WE16), .out_20(WE17), .out_21(WE18), .out_22(WE19),
    .out_23(WE20), .out_24(WE21), .out_25(WE22), .out_26(WE23), .out_27(WE24), .out_28(WE25), .out_29(WE26),
    .out_30(WE27), .out_31(WE28), .out_32(WE29), .out_33(WE30), .out_34(WE31));
  Register #(.width(32)) u__1 (.D(WD), .en(WE1), .Q(_1), .clk(clk), .clr(reset));
  Register #(.width(32)) u__2 (.D(WD), .en(WE2), .Q(_2), .clk(clk), .clr(reset));
  Register #(.width(32)) u__3 (.D(WD), .en(WE3), .Q(_3), .clk(clk), .clr(reset));
  Register #(.width(32)) u__4 (.D(WD), .en(WE4), .Q(_4), .clk(clk), .clr(reset));
  Register #(.width(32)) u__5 (.D(WD), .en(WE5), .Q(_5), .clk(clk), .clr(reset));
  Register #(.width(32)) u__0 (.D(WD), .en(1'b0), .Q(_0), .clk(clk), .clr(reset));
  Register #(.width(32)) u__6 (.D(WD), .en(WE6), .Q(_6), .clk(clk), .clr(reset));
  Register #(.width(32)) u__7 (.D(WD), .en(WE7), .Q(_7), .clk(clk), .clr(reset));
  Register #(.width(32)) u__8 (.D(WD), .en(WE8), .Q(_8), .clk(clk), .clr(reset));
  Register #(.width(32)) u__9 (.D(WD), .en(WE9), .Q(_9), .clk(clk), .clr(reset));
  Register #(.width(32)) u__10 (.D(WD), .en(WE10), .Q(_10), .clk(clk), .clr(reset));
  Register #(.width(32)) u__11 (.D(WD), .en(WE11), .Q(_11), .clk(clk), .clr(reset));
  Register #(.width(32)) u__12 (.D(WD), .en(WE12), .Q(_12), .clk(clk), .clr(reset));
  Register #(.width(32)) u__13 (.D(WD), .en(WE13), .Q(_13), .clk(clk), .clr(reset));
  Register #(.width(32)) u__14 (.D(WD), .en(WE14), .Q(_14), .clk(clk), .clr(reset));
  Register #(.width(32)) u__15 (.D(WD), .en(WE15), .Q(_15), .clk(clk), .clr(reset));
  Register #(.width(32)) u__16 (.D(WD), .en(WE16), .Q(_16), .clk(clk), .clr(reset));
  Register #(.width(32)) u__17 (.D(WD), .en(WE17), .Q(_17), .clk(clk), .clr(reset));
  Register #(.width(32)) u__18 (.D(WD), .en(WE18), .Q(_18), .clk(clk), .clr(reset));
  Register #(.width(32)) u__19 (.D(WD), .en(WE19), .Q(_19), .clk(clk), .clr(reset));
  Register #(.width(32)) u__20 (.D(WD), .en(WE20), .Q(_20), .clk(clk), .clr(reset));
  Register #(.width(32)) u__21 (.D(WD), .en(WE21), .Q(_21), .clk(clk), .clr(reset));
  Register #(.width(32)) u__22 (.D(WD), .en(WE22), .Q(_22), .clk(clk), .clr(reset));
  Register #(.width(32)) u__23 (.D(WD), .en(WE23), .Q(_23), .clk(clk), .clr(reset));
  Register #(.width(32)) u__24 (.D(WD), .en(WE24), .Q(_24), .clk(clk), .clr(reset));
  Register #(.width(32)) u__25 (.D(WD), .en(WE25), .Q(_25), .clk(clk), .clr(reset));
  Multiplexer #(.select(5), .width(32)) multiplexer_1 (
    .in0(_0), .in1(_1), .in2(_2), .in3(_3), .in4(_4), .in5(_5), .in6(_6), .in7(_7), .in8(_8), .in9(_9),
    .in10(_10), .in11(_11), .in12(_12), .in13(_13), .in14(_14), .in15(_15), .in16(_16), .in17(_17),
    .in18(_18), .in19(_19), .in20(_20), .in21(_21), .in22(_22), .in23(_23), .in24(_24), .in25(_25),
    .in26(_26), .in27(_27), .in28(_28), .in29(_29), .in30(_30), .in31(_31), .out(RD1), .sel(A1));  // open: en
  Register #(.width(32)) u__26 (.D(WD), .en(WE26), .Q(_26), .clk(clk), .clr(reset));
  Register #(.width(32)) u__27 (.D(WD), .en(WE27), .Q(_27), .clk(clk), .clr(reset));
  Register #(.width(32)) u__28 (.D(WD), .en(WE28), .Q(_28), .clk(clk), .clr(reset));
  Register #(.width(32)) u__29 (.D(WD), .en(WE29), .Q(_29), .clk(clk), .clr(reset));
  Register #(.width(32)) u__30 (.D(WD), .en(WE30), .Q(_30), .clk(clk), .clr(reset));
  Register #(.width(32)) u__31 (.D(WD), .en(WE31), .Q(_31), .clk(clk), .clr(reset));
  Multiplexer #(.select(5), .width(32)) multiplexer_2 (
    .in0(_0), .in1(_1), .in2(_2), .in3(_3), .in4(_4), .in5(_5), .in6(_6), .in7(_7), .in8(_8), .in9(_9),
    .in10(_10), .in11(_11), .in12(_12), .in13(_13), .in14(_14), .in15(_15), .in16(_16), .in17(_17),
    .in18(_18), .in19(_19), .in20(_20), .in21(_21), .in22(_22), .in23(_23), .in24(_24), .in25(_25),
    .in26(_26), .in27(_27), .in28(_28), .in29(_29), .in30(_30), .in31(_31), .out(RD2), .sel(A2));  // open: en
endmodule

module get_WE (
  input  WE,
  input  [4:0] in_2,
  output out_3,
  output out_4,
  output out_5,
  output out_6,
  output out_7,
  output out_8,
  output out_9,
  output out_10,
  output out_11,
  output out_12,
  output out_13,
  output out_14,
  output out_15,
  output out_16,
  output out_17,
  output out_18,
  output out_19,
  output out_20,
  output out_21,
  output out_22,
  output out_23,
  output out_24,
  output out_25,
  output out_26,
  output out_27,
  output out_28,
  output out_29,
  output out_30,
  output out_31,
  output out_32,
  output out_33,
  output out_34
);

  wire _0, _1, _2, _3, _4, _5, _6, _7, _8, _9, _10, _11, _12, _13, _14, _15, _16, _17, _18, _19, _20, _21,
       _22, _23, _24, _25, _26, _27, _28, _29, _30, _31, undriven;

  Decoder #(.select(5)) decoder_1 (
    .out0(_0), .out1(_1), .out2(_2), .out3(_3), .out4(_4), .out5(_5), .out6(_6), .out7(_7), .out8(_8),
    .out9(_9), .out10(_10), .out11(_11), .out12(_12), .out13(_13), .out14(_14), .out15(_15), .out16(_16),
    .out17(_17), .out18(_18), .out19(_19), .out20(_20), .out21(_21), .out22(_22), .out23(_23), .out24(_24),
    .out25(_25), .out26(_26), .out27(_27), .out28(_28), .out29(_29), .out30(_30), .out31(_31), .sel(in_2),
    .en(undriven));
  and and_1 (out_3, WE, _0);
  and and_2 (out_4, WE, _1);
  and and_3 (out_5, WE, _2);
  and and_4 (out_6, WE, _3);
  and and_5 (out_7, WE, _4);
  and and_6 (out_8, WE, _5);
  and and_7 (out_9, WE, _6);
  and and_8 (out_10, WE, _7);
  and and_9 (out_11, WE, _8);
  and and_10 (out_12, WE, _9);
  and and_11 (out_13, WE, _10);
  and and_12 (out_14, WE, _11);
  and and_13 (out_15, WE, _12);
  and and_14 (out_16, WE, _13);
  and and_15 (out_17, WE, _14);
  and and_16 (out_18, WE, _15);
  and and_17 (out_19, WE, _16);
  and and_18 (out_20, WE, _17);
  and and_19 (out_21, WE, _18);
  and and_20 (out_22, WE, _19);
  and and_21 (out_23, WE, _20);
  and and_22 (out_24, WE, _21);
  and and_23 (out_25, WE, _22);
  and and_24 (out_26, WE, _23);
  and and_25 (out_27, WE, _24);
  and and_26 (out_28, WE, _25);
  and and_27 (out_29, WE, _26);
  and and_28 (out_30, WE, _27);
  and and_29 (out_31, WE, _28);
  and and_30 (out_32, WE, _29);
  and and_31 (out_33, WE, _30);
  and and_32 (out_34, WE, _31);
endmodule
