// Logisim project Q4_FSM.circ as structural Verilog: 3 circuits, main circuit get_output
module get_output (
  input  in1,
  input  in0,
  input  now1,
  input  now0,
  output \output 
);

  wire not_1_out, not_2_out;

  not not_1 (not_1_out, in0);
  and and_1 (\output , not_1_out, now1, not_2_out);
  not not_2 (not_2_out, now0);
endmodule

module fsm (
  input  CLR,
  input  [1:0] in,
  output Z
);

  wire clock_1_out, clock_2_out, next0, next1, now0, now1;

  Register #(.width(1)) u_now1 (.D(next1), .Q(now1), .clk(clock_1_out));  // open: en, clr
  Clock clock_1 (.out(clock_1_out));
  Register #(.width(1)) u_now0 (.D(next0), .Q(now0), .clk(clock_2_out));  // open: en, clr
  Clock clock_2 (.out(clock_2_out));
  next next_1 (.in1(in[1]), .in0(in[0]), .now1(now1), .now0(now0), .clr(CLR), .next1(next1), .next0(next0));
  get_output get_output_1 (.in1(in[1]), .in0(in[0]), .now1(now1), .now0(now0), .\output (Z));
endmodule

module next (
  input  in1,
  input  in0,
  input  now1,
  input  now0,
  input  clr,
  output next1,
  output next0
);

  wire and_1_out, and_2_out, and_3_out, not_1_out, not_2_out, not_3_out, not_4_out, not_5_out, not_6_out,
       not_7_out, or_1_out;

  not not_1 (not_1_out, clr);
  not not_2 (not_2_out, in0);
  not not_3 (not_3_out, now1);
  and and_1 (and_1_out, not_2_out, not_3_out, now0);
  not not_4 (not_4_out, in1);
  and and_2 (and_2_out, not_4_out, in0, not_5_out);
  not not_5 (not_5_out, now1);
  not not_6 (not_6_out, in1);
  and and_3 (and_3_out, not_6_out, in0, not_7_out);
  not not_7 (not_7_out, now0);
  or or_1 (or_1_out, and_2_out, and_3_out);
  and and_4 (next1, and_1_out, not_1_out);
  and and_5 (next0, or_1_out, not_1_out);
endmodule
