// Logisim project Singal_cycle.circ as structural Verilog: 8 circuits, main circuit main
module main (
  input  reset,
  output [31:0] out_2,
  output out_3,
  output [4:0] out_4,
  output [31:0] out_5,
  output out_6,
  output [4:0] out_7,
  output [31:0] out_8
);

  wire ALUB_MUXOp, clk, comparator_1_eq;
  wire [0:0] and_1_out;
  wire [1:0] GRFA3_MUXOp, GRFWD_MUXOp, IFUIMM_MUXOp, NPCOp;
  wire [2:0] ALUOp, EXTOp;
  wire [31:0] adder_1_out, ALU, DM, EXT, multiplexer_1_out, multiplexer_4_out, PC, RD1;

  Clock u_clk (.out(clk));
  Comparator #(.width(32)) comparator_1 (.a({32{1'b0}}), .b(ALU), .eq(comparator_1_eq));  // open: gt, lt
  Multiplexer #(.select(2), .width(32), .enable("false")) multiplexer_1 (
    .in0(EXT), .in1({PC[31:28], out_2[25:0], 2'b00}), .in2(RD1), .out(multiplexer_1_out), .sel(IFUIMM_MUXOp));  // open: in3
  and and_1 (and_1_out[0], NPCOp[0], comparator_1_eq);
  IFU ifu_1 (
    .NPCIMM(multiplexer_1_out), .clk(clk), .reset(reset), .NPCOp({NPCOp[1], and_1_out[0]}), .PC(PC),
    .IM(out_2));
  controller controller_1 (
    .opcode(out_2[31:26]), .func(out_2[5:0]), .NPCOp(NPCOp), .GRFWE(out_3), .ALUOp(ALUOp), .EXTOp(EXTOp),
    .DMOp(out_6), .GRFA3_MUXOp(GRFA3_MUXOp), .GRFWD_MUXOp(GRFWD_MUXOp), .ALUB_MUXOp(ALUB_MUXOp),
    .NPCIMM_MUXOp(IFUIMM_MUXOp));
  Adder #(.width(32)) adder_1 (.a(PC), .b(32'h4), .out(adder_1_out));  // open: cin, cout
  Multiplexer #(.select(2), .width(5), .enable("false")) multiplexer_2 (
    .in0(out_2[20:16]), .in1(out_2[15:11]), .in2({5{1'b1}}), .out(out_4), .sel(GRFA3_MUXOp));  // open: in3
  Multiplexer #(.select(2), .width(32), .enable("false")) multiplexer_3 (
    .in0(ALU), .in1(DM), .in2(EXT), .in3(adder_1_out), .out(out_5), .sel(GRFWD_MUXOp));
  Multiplexer #(.width(32), .enable("false")) multiplexer_4 (
    .in0(EXT), .in1(out_8), .out(multiplexer_4_out), .sel(ALUB_MUXOp));
  GRF grf_1 (
    .A1(out_2[25:21]), .A2(out_2[20:16]), .A3(out_4), .WD(out_5), .clk(clk), .reset(reset), .WE(out_3),
    .RD1(RD1), .RD2(out_8));
  ALU alu_1 (.ALUA(RD1), .ALUB(multiplexer_4_out), .ALUOp(ALUOp), .ALU(ALU));
  EXT ext_1 (.EXTIMM(out_2[15:0]), .EXTOp(EXTOp), .EXT(EXT));
  DM dm_1 (.DMA(ALU), .DMD(out_8), .clk(clk), .reset(reset), .DMOp(out_6), .DMA_2(out_7), .out_7(DM));

  // Other names for the same wires on the sheet: A3[4:0] = out_4; DMA[4:0] = out_7; DMOp = out_6; GRFWE = out_3;
  //   IM[31:0] = out_2; opcode[5:0] = out_2[31:26]; func[5:0] = out_2[5:0]; imm[15:0] = out_2[15:0];
  //   index[25:0] = out_2[25:0]; PC__index__00[31:2] = {PC[31:28], out_2[25:0]}; shamt[4:0] = out_2[10:6];
  //   rd[4:0] = out_2[15:11]; rt[4:0] = out_2[20:16]; rs[4:0] = out_2[25:21]; DMD[31:0] = out_8; RD2[31:0] = out_8;
  //   WD[31:0] = out_5
endmodule

module NPC (
  input  [31:0] NPCI,
  input  [31:0] NPCIMM,
  input  [1:0] NPCOp,
  output [31:0] NPC
);

  wire [31:0] adder_1_out, adder_2_out, multiplexer_1_out;

  Adder #(.width(32)) adder_1 (.a(32'h4), .b(NPCI), .out(adder_1_out));  // open: cin, cout
  Adder #(.width(32)) adder_2 (.a(adder_1_out), .b(NPCIMM), .out(adder_2_out));  // open: cin, cout
  Multiplexer #(.width(32), .enable("false")) multiplexer_1 (
    .in0(adder_1_out), .in1(adder_2_out), .out(multiplexer_1_out), .sel(NPCOp[0]));
  Multiplexer #(.width(32), .enable("false")) multiplexer_2 (
    .in0(multiplexer_1_out), .in1(NPCIMM), .out(NPC), .sel(NPCOp[1]));
endmodule

module IFU (
  input  clk,
  input  reset,
  input  [1:0] NPCOp,
  input  [31:0] NPCIMM,
  output [31:0] PC,
  output [31:0] IM
);

  wire comparator_1_eq;
  wire [31:0] npc_1_npc, PC_q;

  Register #(.width(32)) u_PC (.D(npc_1_npc), .Q(PC_q), .clk(clk), .clr(reset));  // open: en
  Comparator #(.width(32), .mode("unsigned")) comparator_1 (
    .a(PC_q), .b({32{1'b0}}), .eq(comparator_1_eq));  // open: gt, lt
  Multiplexer #(.width(32), .enable("false")) multiplexer_1 (
    .in0(PC_q), .in1(32'h3000), .out(PC), .sel(comparator_1_eq));
  NPC npc_1 (.NPCI(PC), .NPCIMM(NPCIMM), .NPCOp(NPCOp), .NPC(npc_1_npc));
  ROM #(.addrWidth(5), .dataWidth(32)) rom_1 (.addr(PC[6:2]), .data(IM));  // open: sel

  // Notes on the sheet:
  //   contents of rom_1 (hex, n*v repeats v):
  //   34010001 210821 1040fffe
endmodule

module GRF (
  input  clk,
  input  reset,
  input  WE,
  input  [4:0] A1,
  input  [4:0] A2,
  input  [4:0] A3,
  input  [31:0] WD,
  output [31:0] RD1,
  output [31:0] RD2
);

  wire WE0, WE1, WE2, WE3, WE4, WE5, WE6, WE7, WE8, WE9, WE10, WE11, WE12, WE13, WE14, WE15, WE16, WE17,
       WE18, WE19, WE20, WE21, WE22, WE23, WE24, WE25, WE26, WE27, WE28, WE29, WE30, WE31;
  wire [4:0] and_1_out;
  wire [31:0] _0, _1, _2, _3, _4, _5, _6, _7, _8, _9, _10, _11, _12, _13, _14, _15, _16, _17, _18, _19, _20,
       _21, _22, _23, _24, _25, _26, _27, _28, _29, _30, _31;

  Decoder #(.select(5), .enable("false")) decoder_1 (
    .out0(WE0), .out1(WE1), .out2(WE2), .out3(WE3), .out4(WE4), .out5(WE5), .out6(WE6), .out7(WE7),
    .out8(WE8), .out9(WE9), .out10(WE10), .out11(WE11), .out12(WE12), .out13(WE13), .out14(WE14),
    .out15(WE15), .out16(WE16), .out17(WE17), .out18(WE18), .out19(WE19), .out20(WE20), .out21(WE21),
    .out22(WE22), .out23(WE23), .out24(WE24), .out25(WE25), .out26(WE26), .out27(WE27), .out28(WE28),
    .out29(WE29), .out30(WE30), .out31(WE31), .sel(and_1_out));
  assign and_1_out = {5{WE}} & A3;  // AND_Gate and_1, 5 bits wide
  Register #(.width(32)) u__1 (.D(WD), .en(WE1), .Q(_1), .clk(clk), .clr(reset));
  Register #(.width(32)) u__2 (.D(WD), .en(WE2), .Q(_2), .clk(clk), .clr(reset));
  Register #(.width(32)) u__3 (.D(WD), .en(WE3), .Q(_3), .clk(clk), .clr(reset));
  Register #(.width(32)) u__4 (.D(WD), .en(WE4), .Q(_4), .clk(clk), .clr(reset));
  Register #(.width(32)) u__5 (.D(WD), .en(WE5), .Q(_5), .clk(clk), .clr(reset));
  Register #(.width(32)) u__0 (.D(WD), .en(1'b0), .Q(_0), .clk(clk), .clr(reset));
  Register #(.width(32)) u__6 (.D(WD), .en(WE6), .Q(_6), .clk(clk), .clr(reset));
  Register #(.width(32)) u__7 (.D(WD), .en(WE7), .Q(_7), .clk(clk), .clr(reset));
  Register #(.width(32)) u__8 (.D(WD), .en(WE8), .Q(_8), .clk(clk), .clr(reset));
  Register #(.width(32)) u__9 (.D(WD), .en(WE9), .Q(_9), .clk(clk), .clr(reset));
  Register #(.width(32)) u__10 (.D(WD), .en(WE10), .Q(_10), .clk(clk), .clr(reset));
  Register #(.width(32)) u__11 (.D(WD), .en(WE11), .Q(_11), .clk(clk), .clr(reset));
  Register #(.width(32)) u__12 (.D(WD), .en(WE12), .Q(_12), .clk(clk), .clr(reset));
  Register #(.width(32)) u__13 (.D(WD), .en(WE13), .Q(_13), .clk(clk), .clr(reset));
  Register #(.width(32)) u__14 (.D(WD), .en(WE14), .Q(_14), .clk(clk), .clr(reset));
  Register #(.width(32)) u__15 (.D(WD), .en(WE15), .Q(_15), .clk(clk), .clr(reset));
  Register #(.width(32)) u__16 (.D(WD), .en(WE16), .Q(_16), .clk(clk), .clr(reset));
  Register #(.width(32)) u__17 (.D(WD), .en(WE17), .Q(_17), .clk(clk), .clr(reset));
  Register #(.width(32)) u__18 (.D(WD), .en(WE18), .Q(_18), .clk(clk), .clr(reset));
  Register #(.width(32)) u__19 (.D(WD), .en(WE19), .Q(_19), .clk(clk), .clr(reset));
  Register #(.width(32)) u__20 (.D(WD), .en(WE20), .Q(_20), .clk(clk), .clr(reset));
  Register #(.width(32)) u__21 (.D(WD), .en(WE21), .Q(_21), .clk(clk), .clr(reset));
  Register #(.width(32)) u__22 (.D(WD), .en(WE22), .Q(_22), .clk(clk), .clr(reset));
  Register #(.width(32)) u__23 (.D(WD), .en(WE23), .Q(_23), .clk(clk), .clr(reset));
  Register #(.width(32)) u__24 (.D(WD), .en(WE24), .Q(_24), .clk(clk), .clr(reset));
  Register #(.width(32)) u__25 (.D(WD), .en(WE25), .Q(_25), .clk(clk), .clr(reset));
  Multiplexer #(.select(5), .width(32), .enable("false")) multiplexer_1 (
    .in0(_0), .in1(_1), .in2(_2), .in3(_3), .in4(_4), .in5(_5), .in6(_6), .in7(_7), .in8(_8), .in9(_9),
    .in10(_10), .in11(_11), .in12(_12), .in13(_13), .in14(_14), .in15(_15), .in16(_16), .in17(_17),
    .in18(_18), .in19(_19), .in20(_20), .in21(_21), .in22(_22), .in23(_23), .in24(_24), .in25(_25),
    .in26(_26), .in27(_27), .in28(_28), .in29(_29), .in30(_30), .in31(_31), .out(RD1), .sel(A1));
  Register #(.width(32)) u__26 (.D(WD), .en(WE26), .Q(_26), .clk(clk), .clr(reset));
  Register #(.width(32)) u__27 (.D(WD), .en(WE27), .Q(_27), .clk(clk), .clr(reset));
  Register #(.width(32)) u__28 (.D(WD), .en(WE28), .Q(_28), .clk(clk), .clr(reset));
  Register #(.width(32)) u__29 (.D(WD), .en(WE29), .Q(_29), .clk(clk), .clr(reset));
  Register #(.width(32)) u__30 (.D(WD), .en(WE30), .Q(_30), .clk(clk), .clr(reset));
  Register #(.width(32)) u__31 (.D(WD), .en(WE31), .Q(_31), .clk(clk), .clr(reset));
  Multiplexer #(.select(5), .width(32), .enable("false")) multiplexer_2 (
    .in0(_0), .in1(_1), .in2(_2), .in3(_3), .in4(_4), .in5(_5), .in6(_6), .in7(_7), .in8(_8), .in9(_9),
    .in10(_10), .in11(_11), .in12(_12), .in13(_13), .in14(_14), .in15(_15), .in16(_16), .in17(_17),
    .in18(_18), .in19(_19), .in20(_20), .in21(_21), .in22(_22), .in23(_23), .in24(_24), .in25(_25),
    .in26(_26), .in27(_27), .in28(_28), .in29(_29), .in30(_30), .in31(_31), .out(RD2), .sel(A2));

  // Other names for the same wires on the sheet: WE_t[4:0] = {5{WE}}
endmodule

module ALU (
  input  [31:0] ALUA,
  input  [31:0] ALUB,
  input  [2:0] ALUOp,
  output [31:0] ALU
);

  wire [31:0] A_B, A_B_t, AorB, multiplexer_1_out, multiplexer_2_out;

  Adder #(.width(32)) adder_1 (.a(ALUA), .b(ALUB), .out(A_B));  // open: cin, cout
  Subtractor #(.width(32)) subtractor_1 (.a(ALUA), .b(ALUB), .out(A_B_t));  // open: bin, bout
  assign AorB = ALUA | ALUB;  // OR_Gate or_1, 32 bits wide
  Multiplexer #(.width(32), .enable("false")) multiplexer_1 (
    .in0({32{1'b0}}), .in1(A_B), .out(multiplexer_1_out), .sel(ALUOp[0]));
  Multiplexer #(.width(32), .enable("false")) multiplexer_2 (
    .in0(A_B_t), .in1(AorB), .out(multiplexer_2_out), .sel(ALUOp[0]));
  Multiplexer #(.width(32), .enable("false")) multiplexer_3 (
    .in0(multiplexer_1_out), .in1(multiplexer_2_out), .out(ALU), .sel(ALUOp[1]));

  // Other names for the same wires on the sheet: A[31:0] = ALUA; B[31:0] = ALUB
endmodule

module EXT (
  input  [15:0] EXTIMM,
  input  [2:0] EXTOp,
  output [31:0] EXT
);

  wire [31:0] multiplexer_1_out, multiplexer_2_out, multiplexer_3_out;

  Multiplexer #(.width(32), .enable("false")) multiplexer_1 (
    .in0({32{1'b0}}), .in1({{16{1'b0}}, EXTIMM}), .out(multiplexer_1_out), .sel(EXTOp[0]));
  Multiplexer #(.width(32), .enable("false")) multiplexer_2 (
    .in0({{17{EXTIMM[15]}}, EXTIMM[14:0]}), .in1({{15{EXTIMM[15]}}, EXTIMM[14:0], 2'b00}),
    .out(multiplexer_2_out), .sel(EXTOp[0]));
  Multiplexer #(.width(32), .enable("false")) multiplexer_3 (
    .in0(multiplexer_1_out), .in1(multiplexer_2_out), .out(multiplexer_3_out), .sel(EXTOp[1]));
  Multiplexer #(.width(32), .enable("false")) multiplexer_4 (
    .in0(multiplexer_3_out), .in1({EXTIMM, {16{1'b0}}}), .out(EXT), .sel(EXTOp[2]));

  // Other names for the same wires on the sheet: high_extend[31:16] = EXTIMM; IMM[15:0] = EXTIMM;
  //   sign_extend[31:0] = {{17{EXTIMM[15]}}, EXTIMM[14:0]}; sign_extend___00[31:2] = {{15{EXTIMM[15]}}, EXTIMM[14:0]};
  //   zero_extend[15:0] = EXTIMM
endmodule

module DM (
  input  clk,
  input  reset,
  input  [31:0] DMA,
  input  [31:0] DMD,
  input  DMOp,
  output [4:0] DMA_2,
  output [31:0] out_7
);

  RAM #(.addrWidth(5), .dataWidth(32), .bus("separate")) ram_1 (
    .addr(DMA[6:2]), .din(DMD), .data(out_7), .str(DMOp), .clk(clk), .ld(1'b1), .clr(reset));  // open: sel

  assign DMA_2 = DMA[6:2];
endmodule

module controller (
  input  [5:0] opcode,
  input  [5:0] func,
  output [1:0] NPCOp,
  output GRFWE,
  output [2:0] ALUOp,
  output [2:0] EXTOp,
  output DMOp,
  output [1:0] GRFA3_MUXOp,
  output [1:0] GRFWD_MUXOp,
  output ALUB_MUXOp,
  output [1:0] NPCIMM_MUXOp
);

  wire ADDU, LW, NOP, not_1_out, not_2_out, not_3_out, not_4_out, not_5_out, not_6_out, not_7_out, not_8_out,
       not_9_out, not_10_out, not_11_out, not_12_out, not_13_out, not_14_out, not_15_out, not_16_out,
       not_17_out, not_18_out, not_19_out, not_20_out, not_21_out, not_22_out, not_23_out, not_24_out,
       not_25_out, not_26_out, not_27_out, not_28_out, not_29_out, not_30_out, not_31_out, not_32_out,
       not_33_out, not_34_out, not_35_out, not_36_out, not_37_out, not_38_out, not_39_out, not_40_out,
       not_41_out, not_42_out, not_43_out, not_44_out, not_45_out, not_46_out, not_47_out, not_48_out,
       not_49_out, not_50_out, not_51_out, not_52_out, not_53_out, not_54_out, not_55_out, not_56_out,
       not_57_out, not_58_out, not_59_out, not_60_out, not_61_out, ORI, SUBU;

  not not_1 (not_1_out, opcode[0]);
  not not_2 (not_2_out, opcode[1]);
  not not_3 (not_3_out, opcode[2]);
  not not_4 (not_4_out, opcode[3]);
  not not_5 (not_5_out, opcode[4]);
  not not_6 (not_6_out, opcode[5]);
  not not_7 (not_7_out, func[1]);
  not not_8 (not_8_out, func[2]);
  not not_9 (not_9_out, func[3]);
  not not_10 (not_10_out, func[4]);
  not not_11 (not_11_out, opcode[0]);
  not not_12 (not_12_out, opcode[1]);
  not not_13 (not_13_out, opcode[2]);
  not not_14 (not_14_out, opcode[3]);
  not not_15 (not_15_out, opcode[4]);
  not not_16 (not_16_out, opcode[5]);
  not not_17 (not_17_out, func[2]);
  not not_18 (not_18_out, func[3]);
  not not_19 (not_19_out, func[4]);
  not not_20 (not_20_out, opcode[0]);
  not not_21 (not_21_out, opcode[1]);
  not not_22 (not_22_out, opcode[2]);
  not not_23 (not_23_out, opcode[3]);
  not not_24 (not_24_out, opcode[4]);
  not not_25 (not_25_out, opcode[5]);
  not not_26 (not_26_out, func[0]);
  not not_27 (not_27_out, func[1]);
  not not_28 (not_28_out, func[2]);
  not not_29 (not_29_out, func[3]);
  not not_30 (not_30_out, func[4]);
  not not_31 (not_31_out, func[5]);
  not not_32 (not_32_out, opcode[0]);
  not not_33 (not_33_out, opcode[1]);
  not not_34 (not_34_out, opcode[2]);
  not not_35 (not_35_out, opcode[3]);
  not not_36 (not_36_out, opcode[4]);
  not not_37 (not_37_out, opcode[5]);
  not not_38 (not_38_out, func[0]);
  not not_39 (not_39_out, func[1]);
  not not_40 (not_40_out, func[2]);
  not not_41 (not_41_out, func[4]);
  not not_42 (not_42_out, func[5]);
  and and_1 (ADDU, not_1_out, not_2_out, not_3_out, not_4_out, not_5_out, not_6_out, func[0], not_7_out, not_8_out, not_9_out, not_10_out, func[5]);
  and and_2 (SUBU, not_11_out, not_12_out, not_13_out, not_14_out, not_15_out, not_16_out, func[0], func[1], not_17_out, not_18_out, not_19_out, func[5]);
  and and_3 (NOP, not_20_out, not_21_out, not_22_out, not_23_out, not_24_out, not_25_out, not_26_out, not_27_out, not_28_out, not_29_out, not_30_out, not_31_out);
  and and_4 (NPCIMM_MUXOp[1], not_32_out, not_33_out, not_34_out, not_35_out, not_36_out, not_37_out, not_38_out, not_39_out, not_40_out, func[3], not_41_out, not_42_out);
  not not_43 (not_43_out, opcode[2]);
  not not_44 (not_44_out, opcode[3]);
  not not_45 (not_45_out, opcode[4]);
  not not_46 (not_46_out, opcode[2]);
  not not_47 (not_47_out, opcode[4]);
  not not_48 (not_48_out, opcode[0]);
  not not_49 (not_49_out, opcode[1]);
  not not_50 (not_50_out, opcode[3]);
  not not_51 (not_51_out, opcode[4]);
  not not_52 (not_52_out, opcode[5]);
  not not_53 (not_53_out, opcode[4]);
  not not_54 (not_54_out, opcode[5]);
  not not_55 (not_55_out, opcode[1]);
  not not_56 (not_56_out, opcode[4]);
  not not_57 (not_57_out, opcode[5]);
  not not_58 (not_58_out, opcode[2]);
  not not_59 (not_59_out, opcode[3]);
  not not_60 (not_60_out, opcode[4]);
  not not_61 (not_61_out, opcode[5]);
  and and_5 (LW, opcode[0], opcode[1], not_43_out, not_44_out, not_45_out, opcode[5]);
  and and_6 (DMOp, opcode[0], opcode[1], not_46_out, opcode[3], not_47_out, opcode[5]);
  and and_7 (NPCOp[0], not_48_out, not_49_out, opcode[2], not_50_out, not_51_out, not_52_out);
  and and_8 (EXTOp[2], opcode[0], opcode[1], opcode[2], opcode[3], not_53_out, not_54_out);
  and and_9 (ORI, opcode[0], not_55_out, opcode[2], opcode[3], not_56_out, not_57_out);
  and and_10 (GRFA3_MUXOp[1], opcode[0], opcode[1], not_58_out, not_59_out, not_60_out, not_61_out);
  or or_1 (NPCOp[1], GRFA3_MUXOp[1], NPCIMM_MUXOp[1]);
  or or_2 (ALUOp[0], ADDU, ORI, LW, DMOp);
  or or_3 (ALUOp[1], SUBU, ORI, NPCOp[0]);
  or or_4 (EXTOp[0], ORI, NPCOp[0]);
  or or_5 (EXTOp[1], LW, DMOp, NPCOp[0]);
  or or_6 (GRFA3_MUXOp[0], ADDU, SUBU);
  or or_7 (GRFWD_MUXOp[0], LW, GRFA3_MUXOp[1]);
  or or_8 (GRFWD_MUXOp[1], EXTOp[2], GRFA3_MUXOp[1]);
  or or_9 (GRFWE, ADDU, SUBU, ORI, LW, EXTOp[2], GRFA3_MUXOp[1]);
  or or_10 (ALUB_MUXOp, ADDU, SUBU, NPCOp[0]);

  assign ALUOp[2] = 1'b0;
  assign NPCIMM_MUXOp[0] = GRFA3_MUXOp[1];

  // Other names for the same wires on the sheet: LUI = EXTOp[2]; fu0 = func[0]; fu1 = func[1]; fu2 = func[2];
  //   fu3 = func[3]; fu4 = func[4]; fu5 = func[5]; JAL = GRFA3_MUXOp[1]; JR = NPCIMM_MUXOp[1]; BEQ = NPCOp[0];
  //   op0 = opcode[0]; op1 = opcode[1]; op2 = opcode[2]; op3 = opcode[3]; op4 = opcode[4]; op5 = opcode[5]; SW = DMOp
endmodule
